// Logisim project 7-SPEED FAN PROJECT (COMBINATIONAL PART).circ as structural Verilog: 1 circuit, main circuit main
module main (
  input  A,
  input  B,
  input  C
);

  wire and_1_out, and_2_out, and_3_out, and_4_out, and_5_out, and_6_out, and_7_out, and_8_out, and_9_out,
       and_10_out, and_11_out, and_12_out, and_13_out, and_14_out, and_15_out, and_16_out, not_1_out,
       not_2_out, not_3_out, or_1_out, or_2_out, or_3_out, or_4_out, or_5_out, or_6_out, or_7_out, or_8_out;

  not not_1 (not_1_out, A);
  not not_2 (not_2_out, B);
  not not_3 (not_3_out, C);
  and and_1 (and_1_out, not_1_out, not_3_out);
  and and_2 (and_2_out, A, C);
  and and_3 (and_3_out, not_2_out, not_3_out);
  and and_4 (and_4_out, B, C);
  and and_5 (and_5_out, not_1_out, B);
  and and_6 (and_6_out, B, not_3_out);
  and and_7 (and_7_out, A, not_2_out, C);
  and and_8 (and_8_out, A, not_2_out);
  and and_9 (and_9_out, A, not_3_out);
  and and_10 (and_10_out, not_1_out, not_2_out, C);
  and and_11 (and_11_out, and_6_out, not_1_out);
  and and_12 (and_12_out, and_5_out, C);
  and and_13 (and_13_out, and_8_out, not_3_out);
  and and_14 (and_14_out, and_8_out, C);
  and and_15 (and_15_out, A, B, not_3_out);
  and and_16 (and_16_out, A, B, C);
  or or_1 (or_1_out, and_1_out, B, and_2_out);
  or or_2 (or_2_out, and_3_out, and_4_out, not_1_out);
  or or_3 (or_3_out, A, not_2_out, C);
  or or_4 (or_4_out, and_1_out, or_5_out);
  or or_5 (or_5_out, and_5_out, and_7_out, and_6_out);
  or or_6 (or_6_out, and_1_out, and_6_out);
  or or_7 (or_7_out, and_3_out, and_8_out, and_9_out);
  or or_8 (or_8_out, and_5_out, and_6_out, and_8_out);
  LED led_1 (.in(and_10_out));
  LED led_2 (.in(and_11_out));
  LED led_3 (.in(and_12_out));
  LED led_4 (.in(and_13_out));
  LED led_5 (.in(and_14_out));
  LED led_6 (.in(and_15_out));
  LED led_7 (.in(and_16_out));
  _7_Segment_Display u_7_segment_display_1 (
    .g(or_8_out), .f(or_7_out), .a(or_1_out), .b(or_2_out), .e(or_6_out), .d(or_4_out), .c(or_3_out));  // open: dp

  // Notes on the sheet:
  //   a
  //   b
  //   c
  //   d
  //   e
  //   f
  //   g
  //   Speed-1
  //   Speed-2
  //   Speed-3
  //   Speed-4
  //   Speed-5
  //   Speed-6
  //   Speed-7
  //   FAN
endmodule
