// Logisim project 7-SPEED FAN PROJECT (FULL CIRCUIT).circ as structural Verilog: 1 circuit, main circuit main
module main (
  input  X
);

  wire and_1_out, and_2_out, and_3_out, and_4_out, and_5_out, and_6_out, and_7_out, and_8_out, and_9_out,
       and_10_out, and_11_out, and_12_out, and_13_out, and_14_out, and_15_out, and_16_out, and_17_out,
       and_18_out, button_1_out, clock_1_out, j_k_ff_1_q, j_k_ff_1_qn, j_k_ff_2_q, j_k_ff_2_qn, j_k_ff_3_q,
       j_k_ff_3_qn, or_1_out, or_2_out, or_3_out, or_4_out, or_5_out, or_6_out, or_7_out, or_8_out;

  Clock clock_1 (.out(clock_1_out));
  Button button_1 (.out(button_1_out));
  and and_1 (and_1_out, j_k_ff_2_q, j_k_ff_3_q, X);
  and and_2 (and_2_out, j_k_ff_3_q, X);
  J_K_Flip_Flop j_k_ff_1 (
    .J(and_1_out), .clk(clock_1_out), .K(and_1_out), .Q(j_k_ff_1_q), .Qn(j_k_ff_1_qn), .reset(button_1_out));  // open: preset, en
  J_K_Flip_Flop j_k_ff_2 (
    .J(and_2_out), .clk(clock_1_out), .K(and_2_out), .Q(j_k_ff_2_q), .Qn(j_k_ff_2_qn), .reset(button_1_out));  // open: preset, en
  J_K_Flip_Flop j_k_ff_3 (
    .J(X), .clk(clock_1_out), .K(X), .Q(j_k_ff_3_q), .Qn(j_k_ff_3_qn), .reset(button_1_out));  // open: preset, en
  and and_3 (and_3_out, j_k_ff_1_q, j_k_ff_3_q);
  or or_1 (or_1_out, and_3_out, and_4_out, j_k_ff_2_q);
  and and_4 (and_4_out, j_k_ff_1_qn, j_k_ff_3_qn);
  and and_5 (and_5_out, j_k_ff_2_qn, j_k_ff_3_qn);
  or or_2 (or_2_out, and_5_out, and_6_out, j_k_ff_1_qn);
  and and_6 (and_6_out, j_k_ff_2_q, j_k_ff_3_q);
  or or_3 (or_3_out, j_k_ff_1_q, j_k_ff_2_qn, j_k_ff_3_q);
  and and_7 (and_7_out, j_k_ff_1_qn, j_k_ff_2_q);
  or or_4 (or_4_out, and_7_out, and_8_out, and_9_out);
  and and_8 (and_8_out, j_k_ff_2_q, j_k_ff_3_qn);
  and and_9 (and_9_out, j_k_ff_1_q, j_k_ff_2_qn, j_k_ff_3_q);
  and and_10 (and_10_out, j_k_ff_1_q, j_k_ff_2_qn);
  and and_11 (and_11_out, j_k_ff_1_q, j_k_ff_3_qn);
  and and_12 (and_12_out, j_k_ff_1_qn, j_k_ff_2_qn, j_k_ff_3_q);
  and and_13 (and_13_out, and_8_out, j_k_ff_1_qn);
  and and_14 (and_14_out, and_7_out, j_k_ff_3_q);
  and and_15 (and_15_out, and_10_out, j_k_ff_3_qn);
  and and_16 (and_16_out, and_10_out, j_k_ff_3_q);
  and and_17 (and_17_out, j_k_ff_1_q, j_k_ff_2_q, j_k_ff_3_qn);
  and and_18 (and_18_out, j_k_ff_1_q, j_k_ff_2_q, j_k_ff_3_q);
  or or_5 (or_5_out, and_4_out, or_4_out);
  or or_6 (or_6_out, and_4_out, and_8_out);
  or or_7 (or_7_out, and_5_out, and_10_out, and_11_out);
  or or_8 (or_8_out, and_7_out, and_8_out, and_10_out);
  LED led_1 (.in(and_12_out));
  LED led_2 (.in(and_13_out));
  LED led_3 (.in(and_14_out));
  LED led_4 (.in(and_15_out));
  LED led_5 (.in(and_16_out));
  LED led_6 (.in(and_17_out));
  LED led_7 (.in(and_18_out));
  _7_Segment_Display u_7_segment_display_1 (
    .g(or_8_out), .f(or_7_out), .a(or_1_out), .b(or_2_out), .e(or_6_out), .d(or_5_out), .c(or_3_out));  // open: dp

  // Notes on the sheet:
  //   Direction
  //   Clock
  //   Clear
  //   B
  //   A'
  //   A
  //   B'
  //   C
  //   C'
  //   a
  //   b
  //   c
  //   d
  //   e
  //   f
  //   g
  //   SPEED-1
  //   SPEED-2
  //   SPEED-3
  //   SPEED-4
  //   SPEED-5
  //   SPEED-6
  //   SPEED-7
  //   FAN
endmodule
