// Logisim project 7-SPEED FAN PROJECT (SEQUENTIAL PART).circ as structural Verilog: 1 circuit, main circuit main
module main (
  input  X,
  output A,
  output A_prime,
  output B,
  output B_prime,
  output C,
  output C_prime
);

  wire and_1_out, and_2_out, button_1_out, clock_1_out;

  Clock clock_1 (.out(clock_1_out));
  Button button_1 (.out(button_1_out));
  and and_1 (and_1_out, B, C, X);
  and and_2 (and_2_out, C, X);
  J_K_Flip_Flop j_k_ff_1 (
    .J(and_1_out), .clk(clock_1_out), .K(and_1_out), .Q(A), .Qn(A_prime), .reset(button_1_out));  // open: preset, en
  J_K_Flip_Flop j_k_ff_2 (
    .J(and_2_out), .clk(clock_1_out), .K(and_2_out), .Q(B), .Qn(B_prime), .reset(button_1_out));  // open: preset, en
  J_K_Flip_Flop j_k_ff_3 (
    .J(X), .clk(clock_1_out), .K(X), .Q(C), .Qn(C_prime), .reset(button_1_out));  // open: preset, en

  // Notes on the sheet:
  //   Direction
  //   Clock
  //   Clear
endmodule
